# Fritzing sketch Juan_Soto_ENV_Project (saved by Fritzing 0.9.3b)
breadboards: 1

parts:
  Water_Level_Sensor1 = Water Level Sensor
  Part1 = Arduino Mega 2560 (Rev3)
  S1 = PH meter [package=THT]
  Part2 = 24 NeoPixel Ring [part_number=1586]
  R1 = Temperature Sensor (Thermistor) [thermistor_type=NTC package=THT]
  R2 = Resistor [tolerance=±5% resistance=220 package="0805 [SMD]"]
  DHT1 = DHT22 Humidity and Temperature Sensor
  R3 = Resistor [tolerance=±5% resistance=220 package="2010 [SMD]"]
  Part3 = SI1145 Digital UV Index + IR + Visible Light Sensor [part_number=1777]
  S2 = PH meter [package=THT]

nets:
  N1: Water_Level_Sensor1.SIG, Part1.A1
  VDD: Water_Level_Sensor1.VCC, Part1.5V, S1.pin2, Part2.VDD, R2.Pin_1, DHT1.VDD, R3.Pin_1, Part3.+5V, S2.pin2
  GND: Water_Level_Sensor1.GND, Part1.GND, S1.pin3, Part2.GND, R1.pin_1, DHT1.GND, Part3.GND, S2.pin3
  N2: Part1.A0, S1.pin1
  N3: Part1.A2, R1.pin_0, R2.Pin_0
  N4: Part1.A3, S2.pin1
  N5: Part1.D21/SCL, Part3.SCL
  N6: Part1.D20/SDA, Part3.SDA
  N7: Part1.D8_PWM, DHT1.DATA, R3.Pin_0
  N8: Part1.D6_PWM, Part2.IN

notes:
  Gravity EC Meter

custom parts:
  Water Level Sensor: A water level sensor. This sensor operates at 3V to 5V. The Sig (signal) pin outputs an analogue signal that is in proportion to the amount of water in contact with the sensor.
  24 NeoPixel Ring: 24 ultra bright smart LED NeoPixels are arranged in a circle with 2.6" (66mm) outer diameter. The rings are 'chainable' - connect the output pin of one to the input pin of another. Use only one microcontroller pin to control as many as you can chain together! Each LED is addressable as the driver chip is inside the LED. Each one has ~18mA constant current drive so the color will be very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
  SI1145 Digital UV Index + IR + Visible Light Sensor: The SI1145 is a new sensor from SiLabs with a calibrated light sensing algorithm that can calculate UV Index. It doesn't contain an actual UV sensing element, instead it approximates it based on visible & IR light from the sun. We took this outside a couple days and compared the calculated UV index with the news-reported index and found it was very accurate! It's a digital sensor that works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
